// Logisim project jpu8.circ as structural Verilog: 2 circuits, main circuit main
module main (
  input  RST,
  input  [7:0] EX_input
);

  wire A_R, A_W, ALU_EN, B_R, B_W, C_R, C_W, CLK, D_R, D_W, EX_R, EX_W, IM_R, MEM_R, MEM_W, XI_W, YI_W, ZO_R;
  wire [2:0] read_addr, write_addr;
  wire [4:0] ALU_CTRL;
  wire [7:0] alu_1_z_output, ALU_XI, ALU_YI, D_BUS, register_1_q, register_2_q, register_3_q, register_5_q,
       register_7_q;

  Clock clock_1 (.out(CLK));
  Counter #(.max('h3), .width(2)) counter_1 (
    .clr(RST), .load(1'b1), .clk(CLK), .D(2'b00));  // open: up, count, carry, Q
  Decoder #(.enable("false"), .select(3)) decoder_1 (
    .out0(A_W), .out1(B_W), .out2(C_W), .out3(D_W), .out4(XI_W), .out5(YI_W), .out6(EX_W), .out7(MEM_W),
    .sel(write_addr));
  Register #(.trigger("high")) register_1 (.D(D_BUS), .en(A_W), .clk(CLK), .Q(register_1_q), .clr(RST));
  Register #(.trigger("high")) register_2 (.D(D_BUS), .en(C_W), .clk(CLK), .Q(register_2_q), .clr(RST));
  Register #(.trigger("high")) register_3 (.D(D_BUS), .en(EX_W), .clk(CLK), .Q(register_3_q), .clr(RST));
  Register #(.trigger("high")) register_4 (.D(D_BUS), .en(XI_W), .clk(CLK), .Q(ALU_XI), .clr(RST));
  assign D_BUS = A_R ? register_1_q : 8'bz;  // Controlled_Buffer controlled_buffer_1
  assign D_BUS = C_R ? register_2_q : 8'bz;  // Controlled_Buffer controlled_buffer_2
  _7_Segment_Display u_7_segment_display_1 ();  // open: g, f, a, b, e, d, c, dp
  // BCD_to_7_Segment_decoder bcd_to_7_segment_decoder_1: pin names not known
  // Binary_to_BCD_converter #(.binvalue(8)) binary_to_bcd_converter_1: pin names not known; wires that end beside it: register_3_q
  _7_Segment_Display u_7_segment_display_2 ();  // open: g, f, a, b, e, d, c, dp
  _7_Segment_Display u_7_segment_display_3 ();  // open: g, f, a, b, e, d, c, dp
  // BCD_to_7_Segment_decoder bcd_to_7_segment_decoder_2: pin names not known
  // BCD_to_7_Segment_decoder bcd_to_7_segment_decoder_3: pin names not known
  ALU alu_1 (.X_input(ALU_XI), .Y_input(ALU_YI), .control_word(ALU_CTRL), .Z_output(alu_1_z_output));
  Decoder #(.select(3)) decoder_2 (
    .out0(A_R), .out1(B_R), .out2(C_R), .out3(D_R), .out4(ZO_R), .out5(IM_R), .out6(EX_R), .out7(MEM_R),
    .sel(read_addr));  // open: en
  Register #(.trigger("high")) register_5 (.D(D_BUS), .en(B_W), .clk(CLK), .Q(register_5_q), .clr(RST));
  Register #(.trigger("high")) register_6 (.D(D_BUS), .en(YI_W), .clk(CLK), .Q(ALU_YI), .clr(RST));
  Register #(.trigger("high")) register_7 (.D(alu_1_z_output), .en(ALU_EN), .clk(CLK), .Q(register_7_q), .clr(RST));
  assign D_BUS = B_R ? register_5_q : 8'bz;  // Controlled_Buffer controlled_buffer_3
  assign D_BUS = ZO_R ? register_7_q : 8'bz;  // Controlled_Buffer controlled_buffer_4
  assign D_BUS = D_R ? EX_input : 8'bz;  // Controlled_Buffer controlled_buffer_5

  // Other names for the same wires on the sheet: Reset = RST

  // Notes on the sheet:
  //   A
  //   C
  //   C
  //   XI
  //   Skriv (bus -> register)
  //   Expansion Port
  //   Läs (register -> bus)
  //   B
  //   ZO
  //   YI
endmodule

module ALU (
  input  [7:0] X_input,
  input  [7:0] Y_input,
  input  [4:0] control_word,
  output [7:0] Z_output
);

  wire [7:0] adder_1_out, bit_extender_1_out, bit_extender_2_out, bit_extender_3_out, multiplexer_1_out,
       or_1_out, undriven, undriven_2, xor_1_out, xor_2_out;

  assign bit_extender_1_out = {{7{control_word[0]}}, control_word[0]};  // Bit_Extender bit_extender_1
  assign bit_extender_2_out = {{7{control_word[1]}}, control_word[1]};  // Bit_Extender bit_extender_2
  assign xor_1_out = X_input ^ bit_extender_1_out;  // XOR_Gate xor_1, 8 bits wide
  assign xor_2_out = bit_extender_2_out ^ Y_input;  // XOR_Gate xor_2, 8 bits wide
  Adder adder_1 (.a(undriven), .b(undriven_2), .out(adder_1_out), .cin(control_word[3]));  // open: cout
  assign or_1_out = xor_1_out | xor_2_out;  // OR_Gate or_1, 8 bits wide
  Multiplexer #(.width(8)) multiplexer_1 (
    .in0(adder_1_out), .in1(or_1_out), .out(multiplexer_1_out), .sel(control_word[2]));
  assign bit_extender_3_out = {{7{control_word[4]}}, control_word[4]};  // Bit_Extender bit_extender_3
  assign Z_output = bit_extender_3_out ^ multiplexer_1_out;  // XOR_Gate xor_3, 8 bits wide

  // Other names for the same wires on the sheet: invert_X = control_word[0]; invert_Y = control_word[1];
  //   operation = control_word[2]; carry_in = control_word[3]; invert_output = control_word[4]
endmodule
